# Fritzing sketch led-controller-schematic (saved by Fritzing 0.9.5d)
circuit board: 8.47cm x 5.64444cm

parts:
  BUTTON7 = Arcade Button (blue)
  BUTTON8 = Arcade Button (blue)
  BUTTON6 = Arcade Button (blue)
  BUTTON5 = Arcade Button (blue)
  BUTTON12 = Arcade Button (blue)
  BUTTON11 = Arcade Button (blue)
  BUTTON4 = Arcade Button (blue)
  BUTTON3 = Arcade Button (blue)
  BUTTON2 = Arcade Button (blue)
  BUTTON1 = Arcade Button (blue)
  BUTTON9 = Arcade Button (blue)
  BUTTON10 = Arcade Button (blue)
  Part1 = BlackBoard v1.1
  Part4 = Modulo Rele Serial
  Part5 = Modulo Rele Serial
  Part2 = Modulo Rele Serial
  U2 = SLIDER [package=slider]
  Power_plug1 = Power plug
  LED1 = smd LED [color="White (6500K)" package="0603 [SMD]"]
  LED2 = smd LED [color="White (6500K)" package="0603 [SMD]"]
  LED3 = smd LED [color="White (6500K)" package="0603 [SMD]"]
  LED4 = smd LED [color="White (6500K)" package="0603 [SMD]"]
  LED5 = smd LED [color="White (6500K)" package="0603 [SMD]"]
  LED6 = smd LED [color="White (6500K)" package="0603 [SMD]"]
  LED7 = smd LED [color="White (6500K)" package="0603 [SMD]"]
  LED8 = smd LED [color="White (6500K)" package="0603 [SMD]"]
  LED9 = smd LED [color="White (6500K)" package="0603 [SMD]"]
  LED10 = smd LED [color="White (6500K)" package="0603 [SMD]"]
  LED11 = smd LED [color="White (6500K)" package="0603 [SMD]"]
  LED12 = smd LED [color="White (6500K)" package="0603 [SMD]"]

nets:
  GND: BUTTON7.no_name_yet#1, BUTTON8.no_name_yet#1, BUTTON6.no_name_yet#1, BUTTON5.no_name_yet#1, BUTTON12.no_name_yet#1, BUTTON11.no_name_yet#1, BUTTON4.no_name_yet#1, BUTTON3.no_name_yet#1, BUTTON2.no_name_yet#1, BUTTON1.no_name_yet#1, BUTTON9.no_name_yet#1, BUTTON10.no_name_yet#1, Part1.GND, Part4.GND, Part5.GND, Part2.GND, U2.A
  N1: BUTTON7.no_name_yet#2, Part1.D7
  N2: BUTTON8.no_name_yet#2, Part1.D6_PWM
  N3: BUTTON6.no_name_yet#2, Part1.D8
  N4: BUTTON5.no_name_yet#2, Part1.D9_PWM
  N5: BUTTON12.no_name_yet#2, Part1.D10_PWM/SS
  N6: BUTTON11.no_name_yet#2, Part1.D11_PWM/MOSI
  N7: BUTTON4.no_name_yet#2, Part1.D2
  N8: BUTTON3.no_name_yet#2, Part1.D3_PWM
  N9: BUTTON2.no_name_yet#2, Part1.D4
  N10: BUTTON1.no_name_yet#2, Part1.D5_PWM
  N11: BUTTON9.no_name_yet#2, Part1.D13/SCK
  N12: BUTTON10.no_name_yet#2, Part1.D12/MISO
  N13: Part1.A0, U2.S
  N14: Part1.A4/SDA, Part4.CLK, Part5.CLK, Part2.CLK
  N15: Part1.A5/SCL, Part2.Data#33
  N16: Part1.5V#87, U2.E
  12V: Part1.VIN, Part4.12V, Part5.12V, Part2.12V
  N17: Part1.TX0, Part1.5V#95
  N18: Part4.NA1, LED4.cathode
  N19: Part4.C1, Part4.C2, Part4.C3, Part4.C4, Part5.C1, Part5.C2, Part5.C3, Part5.C4, Part2.C1, Part2.C2, Part2.C3, Part2.C4, Power_plug1.VCC
  N20: Part4.NA2, LED3.cathode
  N21: Part4.NA3, LED2.cathode
  N22: Part4.Data, Part5.Data#2
  N23: Part4.NA4, LED1.cathode
  N24: Part5.NA1, LED6.cathode
  N25: Part5.NA2, LED7.cathode
  N26: Part5.NA3, LED5.cathode
  N27: Part5.Data#33, Part2.Data#2
  N28: Part5.NA4, LED8.cathode
  N29: Part2.NA1, LED11.cathode
  N30: Part2.NA2, LED10.cathode
  N31: Part2.NA3, LED12.cathode
  N32: Part2.NA4, LED9.cathode
  N33: Power_plug1.GND, LED1.anode, LED2.anode, LED3.anode, LED4.anode, LED5.anode, LED6.anode, LED7.anode, LED8.anode, LED9.anode, LED10.anode, LED11.anode, LED12.anode

notes:
  LED Controller
  by tairape studio
  www.instagram.com/tairape/
  tairapestudio@gmail.com

custom parts:
  Arcade Button (blue): Adafruit Arcade Button (blue)
  BlackBoard v1.1: Esta é a BlackBoard, a placa Arduino compatível fabricada pela RoboCore. Ela foi projetada unindo o melhor das placas Arduino básicas lançadas até hoje, além de algumas melhorias feitas pelos nossos engenheiros. Veja abaixo as vantagens desta placa para a Arduino UNO R3: Suporta maior drenagem de corrente elétrica em seu pino de 5V (suporta um maior número de periféricos ligados a ela, sem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
  Modulo Rele Serial: Precisando controlar diversos relés com seu Arduino, mas está sem muitos pinos para isso? Seus problemas acabaram! Este é o Módulo Relé Serial, um módulo pensado para quem precisa acionar diversas cargas, mas não dispõe de muitas portas. Com este módulo você consegue controlar os quatro relés da placa independentemente utilizando apenas dois pinos do microcontrolador. Através de uma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
